// Digital circuit ALU.dig as structural Verilog
module ALU (
  input  [31:0] A,
  input  [31:0] B,
  input  [2:0] f3,
  input  srai_sub,
  output [31:0] Out
);

  wire [0:0] slt, sltu;
  wire [31:0] add, \and , multiplexer_1_out, multiplexer_2_out, \or , sll, sra, srl, sub, \xor ;

  Add #(.Bits(32)) add_1 (.a(A), .b(B), .c_i(1'b0), .s(add));  // open: c_o
  Sub #(.Bits(32)) sub_1 (.a(A), .b(B), .c_i(1'b0), .s(sub));  // open: c_o
  assign \xor  = A ^ B;  // XOr xor_1, 32 bits wide
  assign \or  = A | B;  // Or or_1, 32 bits wide
  assign \and  = A & B;  // And and_1, 32 bits wide
  BarrelShifter #(.Bits(32)) u_sll (.in(A), .shift({1'b0, B[4:0]}), .out(sll));
  BarrelShifter #(.Bits(32), .direction("right")) u_srl (.in(A), .shift({1'b0, B[4:0]}), .out(srl));
  BarrelShifter #(.Bits(32), .barrelShifterMode("arithmetic"), .direction("right")) u_sra (
    .in(A), .shift({1'b0, B[4:0]}), .out(sra));
  Comparator #(.Bits(32)) u_slt (.a(A), .b(B), .lt(slt[0]));  // open: gt, eq
  Comparator #(.Signed("true"), .Bits(32)) u_sltu (.a(A), .b(B), .lt(sltu[0]));  // open: gt, eq
  Multiplexer #(.Bits(32)) multiplexer_1 (.sel(srai_sub), .in_0(add), .in_1(sub), .out(multiplexer_1_out));
  Multiplexer #(.Bits(32)) multiplexer_2 (.sel(srai_sub), .in_0(sra), .in_1(srl), .out(multiplexer_2_out));
  Multiplexer #(.Selector_Bits(3), .Bits(32)) multiplexer_3 (
    .sel(f3), .in_0(multiplexer_1_out), .in_1(sll), .in_2({{31{1'b0}}, slt[0]}),
    .in_3({{31{1'b0}}, sltu[0]}), .in_4(\xor ), .in_5(\or ), .in_6(\and ), .in_7(multiplexer_2_out), .out(Out));

  // Other names for the same wires on the sheet: f9 = srai_sub
endmodule
