// Digital circuit BranchUnit.dig as structural Verilog
module BranchUnit (
  input  [31:0] r1data,
  input  [31:0] r2data,
  input  [2:0] \type ,
  output rs1_pc,
  output pc_jump
);

  wire comparator_1_eq, comparator_2_eq, comparator_3_eq, comparator_4_eq, comparator_5_lt, comparator_6_eq,
       comparator_7_gt, comparator_8_eq, comparator_9_lt, comparator_10_eq, comparator_11_gt,
       comparator_12_eq, not_1_out, or_1_out, or_2_out;

  Comparator #(.Bits(32)) comparator_1 (.a(r1data), .b(r2data), .eq(comparator_1_eq));  // open: gt, lt
  Comparator #(.Bits(3)) comparator_2 (.a(3'b000), .b(\type ), .eq(comparator_2_eq));  // open: gt, lt
  Comparator #(.Bits(32)) comparator_3 (.a(r1data), .b(r2data), .eq(comparator_3_eq));  // open: gt, lt
  Comparator #(.Bits(3)) comparator_4 (.a(3'b001), .b(\type ), .eq(comparator_4_eq));  // open: gt, lt
  Comparator #(.Bits(32)) comparator_5 (.a(r1data), .b(r2data), .lt(comparator_5_lt));  // open: gt, eq
  Comparator #(.Bits(3)) comparator_6 (.a(3'b100), .b(\type ), .eq(comparator_6_eq));  // open: gt, lt
  Comparator #(.Bits(32)) comparator_7 (.a(r1data), .b(r2data), .gt(comparator_7_gt));  // open: eq, lt
  Comparator #(.Bits(3)) comparator_8 (.a(3'b101), .b(\type ), .eq(comparator_8_eq));  // open: gt, lt
  Comparator #(.Signed("true"), .Bits(32)) comparator_9 (.a(r1data), .b(r2data), .lt(comparator_9_lt));  // open: gt, eq
  Comparator #(.Bits(3)) comparator_10 (.a(3'b110), .b(\type ), .eq(comparator_10_eq));  // open: gt, lt
  Comparator #(.Bits(32)) comparator_11 (.a(r1data), .b(r2data), .gt(comparator_11_gt));  // open: eq, lt
  Comparator #(.Bits(3)) comparator_12 (.a(3'b111), .b(\type ), .eq(comparator_12_eq));  // open: gt, lt
  not not_1 (not_1_out, comparator_3_eq);
  and and_1 (pc_jump, comparator_1_eq, comparator_2_eq);
  and and_2 (pc_jump, not_1_out, comparator_4_eq);
  and and_3 (pc_jump, comparator_5_lt, comparator_6_eq);
  or or_1 (or_1_out, comparator_1_eq, comparator_7_gt);
  and and_4 (pc_jump, comparator_9_lt, comparator_10_eq);
  or or_2 (or_2_out, comparator_1_eq, comparator_11_gt);
  and and_5 (pc_jump, or_1_out, comparator_8_eq);
  and and_6 (pc_jump, or_2_out, comparator_12_eq);

  assign rs1_pc = pc_jump;
endmodule
