// Digital circuit CUnit.dig as structural Verilog
module CUnit (
  input  [31:0] Inst,
  output imm_reg,
  output rfwen,
  output [2:0] func3,
  output srai_sub,
  output [1:0] Wbsel,
  output branch,
  output jal_jalR,
  output [2:0] ImmSrc
);

  wire Tipo_B_eq, Tipo_I_eq, Tipo_L_eq, tipo_R_eq;

  Comparator #(.Bits(7)) tipo_R (.a(Inst[6:0]), .b(7'b0110011), .eq(tipo_R_eq));  // open: gt, lt
  Comparator #(.Bits(7)) Tipo_I (.a(Inst[6:0]), .b(7'b0010011), .eq(Tipo_I_eq));  // open: gt, lt
  Comparator #(.Bits(7)) Tipo_L (.a(Inst[6:0]), .b(7'b0000011), .eq(Tipo_L_eq));  // open: gt, lt
  Comparator #(.Bits(7)) Tipo_B (.a(Inst[31:25]), .b(7'b1100011), .eq(Tipo_B_eq));  // open: gt, lt
  Multiplexer multiplexer_1 (.sel(tipo_R_eq), .in_0(1'b0), .in_1(1'b0), .out(imm_reg));
  Multiplexer multiplexer_2 (.sel(tipo_R_eq), .in_0(1'b0), .in_1(1'b1), .out(rfwen));
  Multiplexer #(.Bits(3)) multiplexer_3 (.sel(tipo_R_eq), .in_0(3'b000), .in_1(Inst[14:12]), .out(func3));
  Multiplexer multiplexer_4 (.sel(tipo_R_eq), .in_0(1'b0), .in_1(Inst[29]), .out(srai_sub));
  Multiplexer #(.Bits(2)) multiplexer_5 (.sel(tipo_R_eq), .in_0(2'b00), .in_1(2'b00), .out(Wbsel));
  Multiplexer multiplexer_6 (.sel(tipo_R_eq), .in_0(1'b0), .in_1(1'b0), .out(branch));
  Multiplexer multiplexer_7 (.sel(tipo_R_eq), .in_0(1'b0), .in_1(1'b0), .out(jal_jalR));
  Multiplexer multiplexer_8 (.sel(Tipo_I_eq), .in_0(1'b0), .in_1(1'b1), .out(imm_reg));
  Multiplexer multiplexer_9 (.sel(Tipo_I_eq), .in_0(1'b0), .in_1(1'b1), .out(rfwen));
  Multiplexer #(.Bits(3)) multiplexer_10 (.sel(Tipo_I_eq), .in_0(3'b000), .in_1(Inst[14:12]), .out(func3));
  Multiplexer multiplexer_11 (.sel(Tipo_I_eq), .in_0(1'b0), .in_1(Inst[29]), .out(srai_sub));
  Multiplexer #(.Bits(2)) multiplexer_12 (.sel(Tipo_I_eq), .in_0(2'b00), .in_1(2'b00), .out(Wbsel));
  Multiplexer multiplexer_13 (.sel(Tipo_I_eq), .in_0(1'b0), .in_1(1'b0), .out(branch));
  Multiplexer multiplexer_14 (.sel(Tipo_I_eq), .in_0(1'b0), .in_1(1'b0), .out(jal_jalR));
  Multiplexer #(.Bits(3)) multiplexer_15 (.sel(Tipo_I_eq), .in_0(3'b000), .in_1(3'b000), .out(ImmSrc));
  Multiplexer multiplexer_16 (.sel(Tipo_L_eq), .in_0(1'b0), .in_1(1'b1), .out(imm_reg));
  Multiplexer multiplexer_17 (.sel(Tipo_L_eq), .in_0(1'b0), .in_1(1'b1), .out(rfwen));
  Multiplexer #(.Bits(3)) multiplexer_18 (.sel(Tipo_L_eq), .in_0(3'b000), .out(func3));  // open: in_1
  Multiplexer multiplexer_19 (.sel(Tipo_L_eq), .in_0(1'b0), .in_1(Inst[29]), .out(srai_sub));
  Multiplexer #(.Bits(2)) multiplexer_20 (.sel(Tipo_L_eq), .in_0(2'b00), .in_1(2'b01), .out(Wbsel));
  Multiplexer multiplexer_21 (.sel(Tipo_L_eq), .in_0(1'b0), .in_1(1'b0), .out(branch));
  Multiplexer multiplexer_22 (.sel(Tipo_L_eq), .in_0(1'b0), .in_1(1'b0), .out(jal_jalR));
  Multiplexer #(.Bits(3)) multiplexer_23 (.sel(Tipo_L_eq), .in_0(3'b000), .in_1(3'b000), .out(ImmSrc));
  Multiplexer multiplexer_24 (.sel(Tipo_B_eq), .in_0(1'b0), .in_1(1'b1), .out(imm_reg));
  Multiplexer multiplexer_25 (.sel(Tipo_B_eq), .in_0(1'b0), .in_1(1'b1), .out(rfwen));
  Multiplexer #(.Bits(3)) multiplexer_26 (.sel(Tipo_B_eq), .in_0(3'b000), .out(func3));  // open: in_1
  Multiplexer multiplexer_27 (.sel(Tipo_B_eq), .in_0(1'b0), .in_1(Inst[4]), .out(srai_sub));
  Multiplexer #(.Bits(2)) multiplexer_28 (.sel(Tipo_B_eq), .in_0(2'b00), .in_1(2'b01), .out(Wbsel));
  Multiplexer multiplexer_29 (.sel(Tipo_B_eq), .in_0(1'b0), .in_1(1'b1), .out(branch));
  Multiplexer multiplexer_30 (.sel(Tipo_B_eq), .in_0(1'b0), .in_1(1'b0), .out(jal_jalR));
  Multiplexer #(.Bits(3)) multiplexer_31 (.sel(Tipo_B_eq), .in_0(3'b000), .in_1(3'b101), .out(ImmSrc));
endmodule
