// Digital circuit ImmGen.dig as structural Verilog
module ImmGen (
  input  [2:0] ImmSrc,
  input  [31:0] Inst,
  output [31:0] Imm
);

  Multiplexer #(.Selector_Bits(3), .Bits(32)) multiplexer_1 (
    .sel(ImmSrc), .in_0({{20{1'b0}}, Inst[31:20]}), .in_1({{20{1'b0}}, Inst[31:25], Inst[11:7]}),
    .in_2({{20{1'b0}}, Inst[31], Inst[7], Inst[30:25], Inst[11:8]}), .in_3({{12{1'b0}}, Inst[31:12]}),
    .in_4({{12{1'b0}}, Inst[31], Inst[19:12], Inst[20], Inst[30:21]}), .in_5({32{1'b0}}), .in_6({32{1'b0}}),
    .in_7({32{1'b0}}), .out(Imm));

  // Notes on the sheet:
  //   Inst: Instruccion con inmediato
endmodule
