// Digital circuit Inst-Memory.dig as structural Verilog
module Inst_Memory (
  input  [31:0] Addr,
  output [31:0] Inst
);

  wire [23:0] add_1_s, add_2_s, add_3_s;

  ROM #(.AddrBits(24), .isProgramMemory("true"), .Bits(8)) rom_1 (.A(Addr[23:0]), .sel(1'b1), .D(Inst[31:24]));
  Add #(.Bits(24)) add_1 (.a(Addr[23:0]), .b(24'h1), .c_i(1'b0), .s(add_1_s));  // open: c_o
  ROM #(.AddrBits(24), .Bits(8)) rom_2 (.A(add_1_s), .sel(1'b1), .D(Inst[23:16]));
  Add #(.Bits(24)) add_2 (.a(add_1_s), .b(24'h1), .c_i(1'b0), .s(add_2_s));  // open: c_o
  ROM #(.AddrBits(24), .Bits(8)) rom_3 (.A(add_2_s), .sel(1'b1), .D(Inst[15:8]));
  Add #(.Bits(24)) add_3 (.a(add_2_s), .b(24'h1), .c_i(1'b0), .s(add_3_s));  // open: c_o
  ROM #(.AddrBits(24), .Bits(8)) rom_4 (.A(add_3_s), .sel(1'b1), .D(Inst[7:0]));

  // Notes on the sheet:
  //   Addr: Direccion
  //   contents of rom_1 (hex, n*v repeats v):
  //   a
  //   contents of rom_4 (hex, n*v repeats v):
  //   0,0,0,a
endmodule
