// Digital circuit Monociclo.dig as structural Verilog
module Monociclo (
  input  clk,
  input  in_2
);

  wire dmwen, imm_reg, immgen_1_p3, immgen_1_p4, instdecoder_1_p2, instdecoder_1_p3, instdecoder_1_p4,
       multiplexer_2_out, multiplexer_3_out, pc_jump, registerunit__2_1_p8, rfwen, rs1_pc, srai_sub;
  wire [1:0] Wbsel;
  wire [2:0] data_memory_1_p6, func3, ImmSrc, notconnected_1_out, registerunit__2_1_p3;
  wire [31:0] add_1_s, alu_1_p5, Inst, multiplexer_1_out, PC;

  Multiplexer #(.Bits(32)) multiplexer_1 (.sel(pc_jump), .in_0(add_1_s), .in_1(alu_1_p5), .out(multiplexer_1_out));
  Add #(.Bits(32)) add_1 (.a(PC), .b(32'h4), .c_i(1'b0), .s(add_1_s));  // open: c_o
  PC pc_1 (.\input (multiplexer_1_out), .reset(in_2), .wen(1'b1), .clock(clk), .Output(PC));
  Inst_Memory inst_memory_1 (.Addr(PC), .Inst(Inst));
  // instdecoder instdecoder_1: pin names not known; wires that end beside it: Inst, instdecoder_1_p2, instdecoder_1_p3, instdecoder_1_p4
  // RegisterUnit__2 registerunit__2_1: pin names not known; wires that end beside it: rfwen, instdecoder_1_p2, registerunit__2_1_p3, instdecoder_1_p3, instdecoder_1_p4, clk, PC, registerunit__2_1_p8
  // ImmGen immgen_1: pin names not known; wires that end beside it: ImmSrc, Inst, immgen_1_p3, immgen_1_p4
  CUnit cunit_1 (
    .Inst(Inst), .imm_reg(imm_reg), .rfwen(rfwen), .func3(func3), .srai_sub(srai_sub), .Wbsel(Wbsel),
    .branch(immgen_1_p4), .ImmSrc(ImmSrc));  // open: jal_jalR
  Multiplexer multiplexer_2 (.sel(rs1_pc), .in_0(PC[0]), .in_1(PC[0]), .out(multiplexer_2_out));
  Multiplexer multiplexer_3 (.sel(imm_reg), .in_0(registerunit__2_1_p8), .in_1(immgen_1_p3), .out(multiplexer_3_out));
  // BranchUnit branchunit_1: pin names not known; wires that end beside it: PC, registerunit__2_1_p8, func3, rs1_pc, pc_jump
  // ALU alu_1: pin names not known; wires that end beside it: multiplexer_2_out, multiplexer_3_out, func3, srai_sub, alu_1_p5
  // data_memory data_memory_1: pin names not known; wires that end beside it: alu_1_p5, registerunit__2_1_p8, clk, dmwen, func3, data_memory_1_p6
  // NotConnected on notconnected_1_out[0]
  Multiplexer #(.Bits(3), .Selector_Bits(2)) multiplexer_4 (
    .sel(Wbsel), .in_0(alu_1_p5[2:0]), .in_1(data_memory_1_p6), .in_2(add_1_s[2:0]),
    .in_3(notconnected_1_out), .out(registerunit__2_1_p3));
  // Pins of 1 and 32 bits meet at PC
  // Pins of 3 and 32 bits meet at add_1_s
  // Pins of 3 and 32 bits meet at alu_1_p5
  // Pins of 1 and 3 bits meet at notconnected_1_out

  // Other names for the same wires on the sheet: clock = clk; reset = in_2
endmodule
