// Digital circuit PC.dig as structural Verilog
module PC (
  input  [31:0] ALU,
  input  C,
  input  abs,
  input  rel,
  output [31:0] Next,
  output [31:0] PC
);

  wire Reset_out;
  wire [31:0] Add_ALU_s, multiplexer_1_out, multiplexer_2_out;
  wire [31:16] undriven;

  Register #(.Bits(32), .isProgramCounter("true")) u_PC (.D(multiplexer_2_out), .C(~C), .en(Reset_out), .Q(PC));
  Reset Reset (.out(Reset_out));
  Add #(.Bits(32)) Add_One (.a(PC), .b({undriven, 16'h1}), .c_i(1'b0), .s(Next));  // open: c_o
  Add #(.Bits(32)) Add_ALU (.a(Next), .b(ALU), .c_i(1'b0), .s(Add_ALU_s));  // open: c_o
  Multiplexer #(.Bits(32)) multiplexer_1 (.sel(rel), .in_0(Next), .in_1(Add_ALU_s), .out(multiplexer_1_out));
  Multiplexer #(.Bits(32)) multiplexer_2 (.sel(abs), .in_0(multiplexer_1_out), .in_1(ALU), .out(multiplexer_2_out));
  // Pins of 16 and 32 bits meet at {undriven, 16'h1}

  // Notes on the sheet:
  //   ALU: Current ALU output, this value is used as address in case 
  //   of a in case of a jump or added to the current address.
  //   {{de Aktuelle ALU Ausgabe, dieser Wert wird im Falle 
  //   eines Sprunges als Adresse übernommen oder zur aktuellen Adresse addiert.}}
  //   Next: Address of the next command to be executed. Can be 
  //   used as a return address to implement a call instruction.
  //   {{de Adresse des nächsten auszuführenden Befehls. 
  //   Kann als Rücksprungadresse verwendet werden, um 
  //   einen Call-Befehl zu implementieren.}}
  //   PC: the current program counter
  //   {{de der aktuelle Programmzähler}}
  //   abs: Triggers a absolute jump.
  //   The value of the ALU input is used as the new address.
  //   {{de Absoluten Sprung auslösen. Der Wert des ALU 
  //   Eingangs wird als neue Adresse verwendet.}}
  //   rel: Triggers a relative jump. The value of the ALU 
  //   input is added to the current address.
  //   {{de relativen Spung auslösen. Der Wert des ALU 
  //   Eingangs wird zur aktuellen Adresse addiert.}}
endmodule
