// Digital circuit alu (1).dig as structural Verilog
module alu__1 (
  input  [2:0] f3,
  input  [6:0] f7,
  input  [31:0] op_1,
  input  [31:0] op_2,
  output [31:0] out_3
);

  wire f7r, slt_lt, sltu_lt;
  wire [31:0] add, addsub, \and , \or , sll, slt, sltu, sra, srl, srlsra, sub, \xor ;

  Add #(.Bits(32)) add_1 (.a(op_1), .b(op_2), .c_i(1'b0), .s(add));  // open: c_o
  Sub #(.Bits(32)) sub_1 (.a(op_1), .b(op_2), .c_i(1'b0), .s(sub));  // open: c_o
  assign \and  = op_1 & op_2;  // And and_1, 32 bits wide
  assign \or  = op_1 | op_2;  // Or or_1, 32 bits wide
  assign \xor  = op_1 ^ op_2;  // XOr xor_1, 32 bits wide
  Comparator #(.Bits(32)) u_sltu (.a(op_1), .b(op_2), .lt(sltu_lt));  // open: gt, eq
  Comparator #(.Bits(32), .Signed("true")) u_slt (.a(op_1), .b(op_2), .lt(slt_lt));  // open: gt, eq
  BitExtender #(.inputBits(1), .outputBits(32)) bitextender_1 (.in(sltu_lt), .out(sltu));
  BitExtender #(.inputBits(1), .outputBits(32)) bitextender_2 (.in(slt_lt), .out(slt));
  BarrelShifter #(.Bits(32)) u_sll (.in(op_1), .shift(op_2[5:0]), .out(sll));
  BarrelShifter #(.Bits(32), .direction("right")) u_srl (.in(op_1), .shift(op_2[5:0]), .out(srl));
  BarrelShifter #(.Bits(32), .barrelShifterMode("arithmetic"), .direction("right")) u_sra (
    .in(op_1), .shift(op_2[5:0]), .out(sra));
  Comparator #(.Bits(7)) comparator_1 (.a(f7), .b(7'b0100000), .eq(f7r));  // open: gt, lt
  Multiplexer #(.Bits(32)) multiplexer_1 (.sel(f7r), .in_0(add), .in_1(sub), .out(addsub));
  Multiplexer #(.Bits(32)) multiplexer_2 (.sel(f7r), .in_0(srl), .in_1(sra), .out(srlsra));
  Multiplexer #(.Bits(32), .Selector_Bits(3)) multiplexer_3 (
    .sel(f3), .in_0(addsub), .in_1(srlsra), .in_2(\and ), .in_3(\or ), .in_4(\xor ), .in_5(slt), .in_6(sltu),
    .in_7(sll), .out(out_3));
  // Probe Dec on out_3
endmodule
