// Digital circuit control.dig as structural Verilog
module control (
  input  [31:0] Inst,
  output Imm_reg,
  output rfwrenable,
  output [2:0] Funct3,
  output sra_i_sub,
  output [6:0] Opcode,
  output dmwrenable
);

  wire type_B_eq, type_R_eq;
  wire [6:1] undriven;

  Comparator #(.Bits(7)) type_R (.a(Inst[6:0]), .b(7'b0110011), .eq(type_R_eq));  // open: gt, lt
  Comparator #(.Bits(7)) type_S (.a(Inst[6:0]), .b(7'b0100011), .eq(dmwrenable));  // open: gt, lt
  Comparator #(.Bits(7)) type_B (.a(Inst[6:0]), .b(7'b1100011), .eq(type_B_eq));  // open: gt, lt
  Comparator #(.Bits(7)) type_B_2 (.a(Inst[6:0]), .b({undriven, 1'b1}));  // open: gt, eq, lt
  not not_1 (Imm_reg, type_R_eq);
  nor nor_1 (rfwrenable, dmwrenable, type_B_eq);
  // Pins of 1 and 7 bits meet at {undriven, 1'b1}

  assign Funct3 = Inst[14:12];
  assign Opcode = Inst[6:0];
  assign sra_i_sub = Inst[30];
endmodule
