// Digital circuit data memory.dig as structural Verilog
module data_memory (
  input  load,
  input  [31:0] rwaddr,
  input  [31:0] wdata,
  input  clock,
  input  dmwen,
  input  [2:0] fun3,
  output [31:0] out,
  output [31:0] outread
);

  wire and_1_out, and_2_out, and_3_out, and_4_out, comparator_1_eq, comparator_2_eq, comparator_3_eq,
       or_1_out, or_2_out;

  Comparator #(.Bits(3)) comparator_1 (.a(3'b010), .b(fun3), .eq(comparator_1_eq));  // open: gt, lt
  Comparator #(.Bits(3)) comparator_2 (.a(3'b001), .b(fun3), .eq(comparator_2_eq));  // open: gt, lt
  Comparator #(.Bits(3)) comparator_3 (.a(3'b000), .b(fun3), .eq(comparator_3_eq));  // open: gt, lt
  and and_1 (and_1_out, dmwen, or_1_out);
  or or_1 (or_1_out, comparator_1_eq, comparator_2_eq, comparator_3_eq);
  BlockRAMDualPort #(.AddrBits(24), .Bits(8)) byte0 (
    .A(rwaddr[23:0]), .Din(wdata[7:0]), .str(and_1_out), .C(clock), .D(out[7:0]));
  and and_2 (and_2_out, dmwen, or_2_out);
  or or_2 (or_2_out, comparator_1_eq, comparator_2_eq);
  BlockRAMDualPort #(.AddrBits(24), .Bits(8)) byte1 (
    .A(rwaddr[23:0]), .Din(wdata[15:8]), .str(and_2_out), .C(clock), .D(out[15:8]));
  and and_3 (and_3_out, dmwen, comparator_1_eq);
  BlockRAMDualPort #(.AddrBits(24), .Bits(8)) byte2 (
    .A(rwaddr[23:0]), .Din(wdata[23:16]), .str(and_3_out), .C(clock), .D(out[23:16]));
  and and_4 (and_4_out, dmwen, comparator_1_eq);
  BlockRAMDualPort #(.AddrBits(24), .Bits(8)) byte3 (
    .A(rwaddr[23:0]), .Din(wdata[31:24]), .str(and_4_out), .C(clock), .D(out[31:24]));
  Multiplexer #(.Bits(8)) multiplexer_1 (
    .sel(comparator_1_eq), .in_0({8{1'b0}}), .in_1(out[31:24]), .out(outread[31:24]));
  Multiplexer #(.Bits(8)) multiplexer_2 (
    .sel(comparator_1_eq), .in_0({8{1'b0}}), .in_1(out[23:16]), .out(outread[23:16]));
  Multiplexer #(.Bits(8)) multiplexer_3 (.sel(or_2_out), .in_0({8{1'b0}}), .in_1(out[15:8]), .out(outread[15:8]));
  Multiplexer #(.Bits(8)) multiplexer_4 (.sel(or_1_out), .in_0({8{1'b0}}), .in_1(out[7:0]), .out(outread[7:0]));

  // Notes on the sheet:
  //   outread: read
endmodule
