// Digital circuit immediate.dig as structural Verilog
module immediate (
  input  [31:0] Inst,
  output [31:0] Imm_I,
  output [31:0] imm_S,
  output [4:0] shamt_I,
  output srai_srli,
  output [31:0] imm_B,
  output [31:0] imm_U,
  output [31:0] imm_J
);

  BitExtender #(.inputBits(1), .outputBits(20)) bitextender_1 (.in(Inst[31]), .out(Imm_I[31:12]));
  BitExtender #(.inputBits(1), .outputBits(11)) bitextender_2 (.in(Inst[31]), .out(imm_J[31:21]));
  BitExtender #(.inputBits(1), .outputBits(20)) bitextender_3 (.in(Inst[31]), .out(imm_S[31:12]));
  BitExtender #(.inputBits(1), .outputBits(19)) bitextender_4 (.in(Inst[31]), .out(imm_B[31:13]));
  BitExtender #(.inputBits(1), .outputBits(12)) bitextender_5 (.in(1'b0), .out(imm_U[11:0]));

  assign imm_B[12:0] = {Inst[31], Inst[7], Inst[30:25], Inst[11:8], 1'b0};
  assign Imm_I[11:0] = Inst[31:20];
  assign imm_J[20:0] = {Inst[31], Inst[19:12], Inst[20], Inst[30:21], 1'b0};
  assign imm_S[11:0] = {Inst[31:25], Inst[11:7]};
  assign imm_U[31:12] = Inst[31:12];
  assign shamt_I = Inst[24:20];
  assign srai_srli = Inst[30];
endmodule
